// Logisim project computer.circ as structural Verilog: 13 circuits, main circuit alu
module alu (
  input  [7:0] A,
  input  [7:0] B,
  input  sel0,
  input  sel1,
  input  sel2,
  input  sel3,
  output [7:0] F,
  output CARRY_OUT,
  output EQ,
  output A_ZERO
);

  wire ALU_CARRY_IN0, ALU_CARRY_IN1, ALU_S0, ALU_S0_un, ALU_S1, ALU_S1_un, ALU_S2, ALU_S2_un, and_1_out,
       and_2_out, and_3_out, and_4_out, fAND, ffOR, fNOT, fSHIFT, fSUB, fSUM, fXOR, nand_1_out, not_1_out,
       not_2_out, not_3_out, not_4_out, not_5_out, not_6_out, not_7_out, not_8_out, not_11_out, not_12_out,
       not_13_out, not_14_out, or_1_out, or_2_out, or_3_out, or_4_out, or_5_out, or_6_out, or_7_out,
       or_8_out, or_9_out, or_10_out, or_12_out, or_13_out;

  // _74181 #(.ShowInternalStructure("true")) 74181_1: pin names not known; wires that end beside it: B[0], A[0], sel1, ALU_S2, ALU_S1, ALU_S0, ALU_CARRY_IN0, sel2, F[0], F[1], F[2], A[1], B[1], A[2], B[2], A[3], B[3], ALU_CARRY_IN1, EQ, F[3]
  or or_1 (or_1_out, A[0], A[1]);
  or or_2 (or_2_out, A[2], A[3]);
  or or_3 (or_3_out, A[4], A[5]);
  or or_4 (or_4_out, A[6], A[7]);
  not not_1 (not_1_out, A[0]);
  not not_2 (not_2_out, A[1]);
  not not_3 (not_3_out, A[2]);
  not not_4 (not_4_out, A[3]);
  not not_5 (not_5_out, A[4]);
  not not_6 (not_6_out, A[5]);
  not not_7 (not_7_out, A[6]);
  not not_8 (not_8_out, A[7]);
  or or_5 (or_5_out, or_1_out, or_2_out);
  or or_6 (or_6_out, or_5_out, or_7_out);
  or or_7 (or_7_out, or_3_out, or_4_out);
  nand nand_1 (nand_1_out, not_1_out, not_2_out, not_3_out, not_4_out, not_5_out, not_6_out, not_7_out, not_8_out);
  // NOT_Gate not_9 has open pins: in=nand_1_out, out=open
  not not_10 (A_ZERO, or_6_out);
  // _74181 #(.ShowInternalStructure("true")) 74181_2: pin names not known; wires that end beside it: B[4], A[4], sel1, ALU_S2, ALU_S1, ALU_S0, ALU_CARRY_IN1, sel2, F[4], F[5], F[6], A[5], B[5], A[6], B[6], A[7], B[7], CARRY_OUT, EQ, F[7]
  Decoder #(.enable("false"), .select(3)) decoder_1 (
    .out0(ALU_CARRY_IN0), .out1(fSUB), .out2(fSHIFT), .out3(fSUM), .out4(fNOT), .out5(fXOR), .out6(ffOR),
    .out7(fAND), .sel({sel2, sel1, sel0}));
  or or_8 (or_8_out, sel0, sel2);
  not not_11 (not_11_out, sel2);
  not not_12 (not_12_out, sel1);
  not not_13 (not_13_out, sel0);
  or or_9 (or_9_out, fNOT, fSUM);
  and and_1 (and_1_out, or_8_out, not_11_out);
  not not_14 (not_14_out, sel1);
  and and_2 (and_2_out, not_14_out, sel2);
  and and_3 (and_3_out, not_12_out, sel0);
  or or_10 (or_10_out, and_3_out, and_4_out);
  and and_4 (and_4_out, sel1, not_13_out);
  and and_5 (ALU_S0_un, sel0, sel1);
  or or_11 (ALU_S2_un, and_2_out, or_10_out);
  or or_12 (or_12_out, or_9_out, fAND);
  or or_13 (or_13_out, or_9_out, fSHIFT);
  or or_14 (ALU_S0, fAND, fSUM);
  or or_15 (ALU_S1_un, and_1_out, and_2_out);
  not not_15 (ALU_S2, or_12_out);
  not not_16 (ALU_S1, or_13_out);

  // Other names for the same wires on the sheet: ALU_S3 = sel1; ALU_S3_un = sel1; ALU_LOGIC = sel2; ALU_A[7:0] = A;
  //   ALU_A0 = A[0]; ALU_A1 = A[1]; ALU_A2 = A[2]; ALU_A3 = A[3]; ALU_A4 = A[4]; ALU_A5 = A[5]; ALU_A6 = A[6];
  //   ALU_A7 = A[7]; ALU_B[7:0] = B; ALU_B0 = B[0]; ALU_B1 = B[1]; ALU_B2 = B[2]; ALU_B3 = B[3]; ALU_B4 = B[4];
  //   ALU_B5 = B[5]; ALU_B6 = B[6]; ALU_B7 = B[7]; ALU_CARRY_OUT0 = ALU_CARRY_IN1; ALU_CARRY_OUT1 = CARRY_OUT;
  //   ALU_EQ0 = EQ; ALU_EQ1 = EQ; ALU_F[7:0] = F; ALU_F0 = F[0]; ALU_F1 = F[1]; ALU_F2 = F[2]; ALU_F3 = F[3];
  //   ALU_F4 = F[4]; ALU_F5 = F[5]; ALU_F6 = F[6]; ALU_F7 = F[7]; fCMP = ALU_CARRY_IN0

  // Notes on the sheet:
  //   eq comp only works if carry in is high and subtract mode
  //   9 inverters, 1 nand, 3 ic's
  //   eq is open collector, can wire AND (?)
  //   7 or, 1 inv, 3 chips (unless inv is around)
  //   1 or chip, 1 inv (could be used for other things as well), 1 dec -> 3 chips
endmodule

module generic_8bit_register (
  input  CLOCK,
  input  WE,
  input  nRESET,
  input  [7:0] D,
  output [7:0] Q
);

  wire fall, n74273_1_pin11, not_1_out, not_2_out, not_3_out, not_4_out, not_5_out, not_6_out, not_7_out,
       RISE;

  not not_1 (not_1_out, CLOCK);
  not not_2 (not_2_out, CLOCK);
  not not_3 (not_3_out, not_2_out);
  not not_4 (not_4_out, CLOCK);
  not not_5 (not_5_out, not_4_out);
  not not_6 (not_6_out, not_5_out);
  and and_1 (fall, not_1_out, not_3_out);
  and and_2 (RISE, CLOCK, not_6_out);
  _74273 u_74273_1 (
    .pin1(nRESET), .pin2(Q[0]), .pin3(D[0]), .pin4(D[1]), .pin5(Q[1]), .pin6(Q[2]), .pin7(D[2]), .pin8(D[3]),
    .pin9(Q[3]), .pin19(Q[7]), .pin18(D[7]), .pin17(D[6]), .pin16(Q[6]), .pin15(Q[5]), .pin14(D[5]),
    .pin13(D[4]), .pin12(Q[4]), .pin11(n74273_1_pin11));
  not not_7 (not_7_out, nRESET);
  and and_3 (n74273_1_pin11, RISE, WE);
  Register register_1 (.D(D), .en(WE), .clk(CLOCK), .clr(not_7_out));  // open: Q

  // Other names for the same wires on the sheet: MR = nRESET

  // Notes on the sheet:
  //   nRESET: initial=0x1
  //   dummy register to get state on the wrapper ic
endmodule

module ALU_assembly (
  input  CLOCK,
  input  [7:0] BIN,
  input  A_WE,
  input  B_WE,
  input  nA_BOUT_EN,
  input  nB_BOUT_EN,
  input  nF_BOUT_EN,
  input  S0,
  input  S1,
  input  S2,
  input  S3,
  input  nRESET,
  output [7:0] BOUT,
  output CARRY_OUT,
  output EQUAL,
  output A_ZERO
);

  wire [3:0] A_REG_q, A_REG_q_2, alu_1_f, alu_1_f_2;
  wire [7:0] B_REG_q;

  Hex_Digit_Display L_A1 (.value(A_REG_q_2));  // open: dp
  Hex_Digit_Display L_A0 (.value(A_REG_q));  // open: dp
  gp_register A_REG (
    .WE(A_WE), .nRESET(nRESET), .CLOCK(CLOCK), .BIN(BIN), .nBOUT_EN(nA_BOUT_EN), .BOUT(BOUT),
    .Q({A_REG_q_2, A_REG_q}));
  gp_register B_REG (
    .WE(B_WE), .nRESET(nRESET), .CLOCK(CLOCK), .BIN(BIN), .nBOUT_EN(nB_BOUT_EN), .BOUT(BOUT), .Q(B_REG_q));
  Hex_Digit_Display L_B1 (.value(A_REG_q_2));  // open: dp
  Hex_Digit_Display L_B0 (.value(A_REG_q));  // open: dp
  Hex_Digit_Display L_F1 (.value(alu_1_f_2));  // open: dp
  // Probe on {alu_1_f_2, alu_1_f}
  alu alu_1 (
    .A({A_REG_q_2, A_REG_q}), .B(B_REG_q), .sel0(S0), .sel1(S1), .sel2(S2), .sel3(S3),
    .F({alu_1_f_2, alu_1_f}), .CARRY_OUT(CARRY_OUT), .EQ(EQUAL), .A_ZERO(A_ZERO));
  Hex_Digit_Display L_F0 (.value(alu_1_f));  // open: dp
  ttl_buffer ttl_buffer_1 (.N_ENABLE(nF_BOUT_EN), .inn({alu_1_f_2, alu_1_f}), .outt(BOUT));

  // Notes on the sheet:
  //   nA_BOUT_EN: initial=0x1
  //   nB_BOUT_EN: initial=0x1
  //   nRESET: initial=0x1
  //   A
  //   B
  //   F
  //   equal cmp: nCARRY_IN = HI (inactive)
endmodule

module ttl_buffer (
  input  N_ENABLE,
  input  [7:0] inn,
  output [7:0] outt
);

  wire not_1_out;

  not not_1 (not_1_out, N_ENABLE);
  _74245 #(.ShowInternalStructure("true")) u_74245_1 (
    .pin1(not_1_out), .pin2(inn[0]), .pin3(inn[1]), .pin4(inn[2]), .pin5(inn[3]), .pin6(inn[4]),
    .pin7(inn[5]), .pin8(inn[6]), .pin9(inn[7]), .pin19(N_ENABLE), .pin18(outt[0]), .pin17(outt[1]),
    .pin16(outt[2]), .pin15(outt[3]), .pin14(outt[4]), .pin13(outt[5]), .pin12(outt[6]), .pin11(outt[7]));
endmodule

module gp_register (
  input  CLOCK,
  input  [7:0] BIN,
  input  WE,
  input  nRESET,
  input  nBOUT_EN,
  output [7:0] BOUT,
  output [7:0] Q
);

  generic_8bit_register generic_8bit_register_1 (.CLOCK(CLOCK), .WE(WE), .nRESET(nRESET), .D(BIN), .Q(Q));
  ttl_buffer ttl_buffer_1 (.N_ENABLE(nBOUT_EN), .inn(Q), .outt(BOUT));
endmodule

module main (
  input  RESET,
  input  in_2,
  input  in_3,
  output [2:0] out_4,
  output [7:0] out_5,
  output [13:0] out_6,
  output [2:0] out_7
);

  wire A_WRITE, A_ZERO, and_1_out, and_2_out, and_3_out, and_4_out, and_5_out, B_WRITE, CARRY, CLK,
       decoder_1_out1, decoder_1_out2, decoder_1_out3, decoder_1_out4, decoder_1_out5, decoder_1_out6,
       decoder_1_out7, decoder_1_out9, decoder_1_out10, decoder_1_out12, decoder_1_out15, decoder_2_out0,
       decoder_2_out1, decoder_2_out2, decoder_2_out3, decoder_3_out0, decoder_3_out6, decoder_3_out7,
       decoder_3_out11, decoder_3_out12, decoder_3_out15, EQUAL, HALT, INV_CLK, IR2_BOUT, IR2_WRITE,
       IR_WRITE, MAR_CNT, MEM_READ, MEM_WRITE, nA_BOUT_EN, nABUS_TO_BUS_HIGH, nABUS_TO_BUS_LOW, nB_BOUT_EN,
       nF_BOUT_EN, nFLAG_BOUT, nMAR_AOUT, nMAR_LOAD_HIGH, nMAR_LOAD_LOW, not_2_out, nPC_AOUT, nPC_LOAD_HIGH,
       nPC_LOAD_LOW, nRESET, nRESET_MICRO, nSP_AOUT, nSP_LOAD_HIGH, nSP_LOAD_LOW, nX_BOUT, nY_BOUT, nZ_BOUT,
       or_1_out, or_2_out, PC_CNT, PC_DIRECT_BASED, PC_FLAG_CARRY_BASED, PC_FLAG_EQ_BASED,
       PC_FLAG_ZERO_BASED, PC_LOAD_HIGH, PC_LOAD_LOW, PC_WRITE_EN, SP_CNTDOWN, SP_CNTUP, X_WRITE, Y_WRITE,
       Z_WRITE;
  wire [1:0] ADDR_CONTROL_DEC;
  wire [3:0] BUS_CONTROL_DEC, BUS_WRITE_DEC, OTHER_DEC;
  wire [3:3] INTRUCTION_CNTR_q;
  wire [7:0] BBUS, dipswitch_1_sw8, Q_FLAGS;
  wire [7:3] IR2_q;
  wire [15:0] ABUS, dipswitch_2_sw16;
  wire [15:14] rom_1_data;

  not not_1 (nRESET, RESET);
  Decoder #(.enable("false"), .select(4)) decoder_1 (
    .out1(decoder_1_out1), .out2(decoder_1_out2), .out3(decoder_1_out3), .out4(decoder_1_out4),
    .out5(decoder_1_out5), .out6(decoder_1_out6), .out7(decoder_1_out7), .out8(MEM_READ),
    .out9(decoder_1_out9), .out10(decoder_1_out10), .out11(IR2_BOUT), .out12(decoder_1_out12), .out13(HALT),
    .out15(decoder_1_out15), .sel(BUS_CONTROL_DEC));  // open: out0, out14
  Decoder #(.enable("false"), .select(2)) decoder_2 (
    .out0(decoder_2_out0), .out1(decoder_2_out1), .out2(decoder_2_out2), .out3(decoder_2_out3),
    .sel(ADDR_CONTROL_DEC));
  Decoder #(.enable("false"), .select(4)) decoder_3 (
    .out0(decoder_3_out0), .out1(A_WRITE), .out2(B_WRITE), .out3(X_WRITE), .out4(Y_WRITE), .out5(Z_WRITE),
    .out6(decoder_3_out6), .out7(decoder_3_out7), .out8(MEM_WRITE), .out9(PC_LOAD_LOW), .out10(PC_LOAD_HIGH),
    .out11(decoder_3_out11), .out12(decoder_3_out12), .out13(IR_WRITE), .out14(IR2_WRITE),
    .out15(decoder_3_out15), .sel(BUS_WRITE_DEC));
  Decoder #(.select(3)) decoder_4 (
    .out0(PC_DIRECT_BASED), .out1(PC_CNT), .out2(MAR_CNT), .out3(SP_CNTUP), .out4(SP_CNTDOWN),
    .out5(PC_FLAG_ZERO_BASED), .out6(PC_FLAG_EQ_BASED), .out7(PC_FLAG_CARRY_BASED), .sel(OTHER_DEC[2:0]),
    .en(not_2_out));
  not not_2 (not_2_out, OTHER_DEC[3]);
  not not_3 (nA_BOUT_EN, decoder_1_out1);
  not not_4 (nB_BOUT_EN, decoder_1_out2);
  not not_5 (nX_BOUT, decoder_1_out3);
  not not_6 (nY_BOUT, decoder_1_out4);
  not not_7 (nZ_BOUT, decoder_1_out5);
  not not_8 (nABUS_TO_BUS_LOW, decoder_1_out6);
  not not_9 (nABUS_TO_BUS_HIGH, decoder_1_out7);
  not not_10 (nF_BOUT_EN, decoder_1_out9);
  not not_11 (nFLAG_BOUT, decoder_1_out10);
  not not_12 (nRESET_MICRO, decoder_1_out15);
  not not_13 (nPC_AOUT, decoder_2_out1);
  not not_14 (nMAR_AOUT, decoder_2_out2);
  not not_15 (nSP_AOUT, decoder_2_out3);
  not not_16 (nMAR_LOAD_LOW, decoder_3_out6);
  not not_17 (nMAR_LOAD_HIGH, decoder_3_out7);
  not not_18 (nSP_LOAD_LOW, decoder_3_out11);
  not not_19 (nSP_LOAD_HIGH, decoder_3_out12);
  Clock clock_1 (.out(CLK));
  not not_20 (INV_CLK, CLK);
  ALU_assembly alu_assembly_1 (
    .B_WE(B_WRITE), .nA_BOUT_EN(nA_BOUT_EN), .nB_BOUT_EN(nB_BOUT_EN), .nF_BOUT_EN(nF_BOUT_EN),
    .A_WE(A_WRITE), .CLOCK(CLK), .BIN(BBUS), .nRESET(nRESET), .S0(OTHER_DEC[0]), .S1(OTHER_DEC[1]),
    .S2(OTHER_DEC[2]), .S3(OTHER_DEC[3]), .CARRY_OUT(CARRY), .EQUAL(EQUAL), .A_ZERO(A_ZERO), .BOUT(BBUS));
  gp_register IR2 (
    .WE(IR2_WRITE), .nRESET(nRESET), .CLOCK(CLK), .BIN(BBUS), .nBOUT_EN(1'b1), .Q({IR2_q, out_4}));  // open: BOUT
  gp_register IR (.WE(IR_WRITE), .nRESET(nRESET), .CLOCK(CLK), .BIN(BBUS), .nBOUT_EN(1'b1), .BOUT(BBUS), .Q(out_5));
  counter4 INTRUCTION_CNTR (
    .nCLEAR(nRESET_MICRO), .CNT_EN(1'b1), .nLOAD_EN(1'b1), .CLOCK(INV_CLK),
    .Q({INTRUCTION_CNTR_q[3], out_6[2:0]}));  // open: D
  ram_assembly ram_assembly_1 (
    .CLOCK(CLK), .BIN(BBUS), .AIN(ABUS), .MEM_READ(MEM_READ), .MEM_WRITE(MEM_WRITE), .nPC_AOUT(nPC_AOUT),
    .PC_CNT(PC_CNT), .nPC_LOAD_LOW(nPC_LOAD_LOW), .nPC_LOAD_HIGH(nPC_LOAD_HIGH), .nMAR_AOUT(nMAR_AOUT),
    .MAR_CNT(MAR_CNT), .nMAR_LOAD_LOW(nMAR_LOAD_LOW), .nMAR_LOAD_HIGH(nMAR_LOAD_HIGH), .nSP_AOUT(nSP_AOUT),
    .nSP_CNTUP(SP_CNTUP), .nSP_CNTDOWN(SP_CNTDOWN), .nSP_LOAD_LOW(nSP_LOAD_LOW),
    .nSP_LOAD_HIGH(nSP_LOAD_HIGH), .nLOW_ATOB_EN(nABUS_TO_BUS_LOW), .nHIGH_ATOB_EN(nABUS_TO_BUS_HIGH),
    .nRESET(nRESET), .BOUT(BBUS), .AOUT(ABUS));
  ROM #(.addrWidth(14), .dataWidth(16)) rom_1 (
    .addr({out_4, out_5, out_6[2:0]}),
    .data({rom_1_data, OTHER_DEC, BUS_WRITE_DEC, ADDR_CONTROL_DEC, BUS_CONTROL_DEC}));
  // LedBar #(.inputtype("row")) ledbar_1: pin names not known; wires that end beside it: BBUS
  DipSwitch dipswitch_1 (
    .sw1(dipswitch_1_sw8[7]), .sw2(dipswitch_1_sw8[6]), .sw3(dipswitch_1_sw8[5]), .sw4(dipswitch_1_sw8[4]),
    .sw5(dipswitch_1_sw8[3]), .sw6(dipswitch_1_sw8[2]), .sw7(dipswitch_1_sw8[1]), .sw8(dipswitch_1_sw8[0]));
  assign BBUS = in_2 ? dipswitch_1_sw8 : 8'bz;  // Controlled_Buffer controlled_buffer_1
  DipSwitch #(.number(16)) dipswitch_2 (
    .sw1(dipswitch_2_sw16[15]), .sw2(dipswitch_2_sw16[14]), .sw3(dipswitch_2_sw16[13]),
    .sw4(dipswitch_2_sw16[12]), .sw5(dipswitch_2_sw16[11]), .sw6(dipswitch_2_sw16[10]),
    .sw7(dipswitch_2_sw16[9]), .sw8(dipswitch_2_sw16[8]), .sw9(dipswitch_2_sw16[7]),
    .sw10(dipswitch_2_sw16[6]), .sw11(dipswitch_2_sw16[5]), .sw12(dipswitch_2_sw16[4]),
    .sw13(dipswitch_2_sw16[3]), .sw14(dipswitch_2_sw16[2]), .sw15(dipswitch_2_sw16[1]),
    .sw16(dipswitch_2_sw16[0]));
  and and_1 (and_1_out, PC_LOAD_LOW, PC_WRITE_EN);
  and and_2 (and_2_out, PC_LOAD_HIGH, PC_WRITE_EN);
  // LedBar #(.inputtype("row"), .matrixcols(16)) ledbar_2: pin names not known; wires that end beside it: ABUS
  and and_3 (and_3_out, PC_FLAG_CARRY_BASED, Q_FLAGS[0]);
  and and_4 (and_4_out, PC_FLAG_EQ_BASED, Q_FLAGS[1]);
  and and_5 (and_5_out, PC_FLAG_ZERO_BASED, Q_FLAGS[2]);
  not not_21 (nPC_LOAD_LOW, and_1_out);
  not not_22 (nPC_LOAD_HIGH, and_2_out);
  gp_register FLAG_REG (
    .WE(nF_BOUT_EN), .nRESET(nRESET), .CLOCK(CLK), .BIN({{5{1'b0}}, A_ZERO, EQUAL, CARRY}),
    .nBOUT_EN(nFLAG_BOUT), .BOUT(BBUS), .Q(Q_FLAGS));
  // LedBar #(.inputtype("row"), .matrixcols(16)) ledbar_3: pin names not known; wires that end beside it: {rom_1_data, OTHER_DEC, BUS_WRITE_DEC, ADDR_CONTROL_DEC, BUS_CONTROL_DEC}
  or or_1 (or_1_out, and_3_out, and_4_out);
  // LedBar #(.inputtype("row"), .matrixcols(4)) ledbar_4: pin names not known; wires that end beside it: BUS_CONTROL_DEC
  // LedBar #(.inputtype("row"), .matrixcols(2)) ledbar_5: pin names not known; wires that end beside it: ADDR_CONTROL_DEC
  assign ABUS = in_3 ? dipswitch_2_sw16 : 16'bz;  // Controlled_Buffer controlled_buffer_2
  or or_2 (or_2_out, or_1_out, and_5_out);
  // LedBar #(.inputtype("row"), .matrixcols(4)) ledbar_6: pin names not known; wires that end beside it: OTHER_DEC
  // LedBar #(.inputtype("row"), .matrixcols(4)) ledbar_7: pin names not known; wires that end beside it: BUS_WRITE_DEC
  or or_3 (PC_WRITE_EN, or_2_out, PC_DIRECT_BASED);

  assign out_6[13:3] = {out_4, out_5};
  assign out_7 = out_6[2:0];

  // Other names for the same wires on the sheet: OTHER_S0 = OTHER_DEC[0]; OTHER_S1 = OTHER_DEC[1];
  //   OTHER_S2 = OTHER_DEC[2]; OTHER_S3 = OTHER_DEC[3]

  // Notes on the sheet:
  //   write from bus decoder
  //   out on bus decoder
  //   other decoder
  //   3 bits of micro instr
  //   contents of rom_1 (hex, n*v repeats v):
  //   358 400 398 441 4*f 358 68 400 5*f 358 621 6*f 358 631 1000 5*f 358 439 c00 5*f 358 400 198 400 1d8
  //   400 f f 358 400 1676 16b7 4*f 72*0 358 400 58 400 4*f 358 400 198 400 1d8 468 f f 358 400 198 400
  //   1d8 621 f f 358 400 398 63b 1000 f f f 358 439 c00 5*f 358 400 198 400 1d8 400 f f 358 276 2b7 5*f
  //   72*0 358 400 398 481 4*f 358 a8 400 5*f 358 622 6*f 358 632 1000 5*f 358 43a c00 5*f 358 400 198 400
  //   1d8 400 f f 358 442 1676 16b7 4*f 72*0 358 400 98 400 4*f 358 400 198 400 1d8 4a8 f f 358 400 198
  //   400 1d8 622 f f 358 400 398 63b 1000 f f f 358 43a c00 5*f 358 400 198 400 1d8 400 f f 358 276 2b7
  //   5*f 72*0 358 400 398 4c1 4*f 358 e8 400 5*f 358 623 6*f 358 633 1000 5*f 358 43b c00 5*f 358 400 198
  //   400 1d8 400 f f 358 443 1676 16b7 4*f 72*0 358 400 d8 400 4*f 358 400 198 400 1d8 4e8 f f 358 400
  //   198 400 1d8 623 f f 358 400 398 63b 1000 f f f 358 43b c00 5*f 358 400 198 400 1d8 400 f f 358 276
  //   2b7 5*f 72*0 358 400 398 501 4*f 358 128 400 5*f 358 624 6*f 358 634 1000 5*f 358 43c c00 5*f 358
  //   400 198 400 1d8 400 f f 358 444 1676 16b7 4*f 72*0 358 400 118 400 4*f 358 400 198 400 1d8 528 f f
  //   358 400 198 400 1d8 624 f f 358 400 398 63b 1000 f f f 358 43c c00 5*f 358 400 198 400 1d8 400 f f
  //   358 276 2b7 5*f 72*0 358 400 398 541 4*f 358 168 400 5*f 358 625 6*f 358 635 1000 5*f 358 43d c00
  //   5*f 358 400 198 400 1d8 400 f f 358 445 1676 16b7 4*f 72*0 358 400 158 400 4*f 358 400 198 400 1d8
  //   568 f f 358 400 198 400 1d8 625 f f 358 400 398 63b 1000 f f f 358 43d c00 5*f 358 400 198 400 1d8
  //   400 f f 358 276 2b7 5*f 72*0 358 400 398 581 4*f 358 1a8 400 5*f 358 626 6*f 358 636 1000 5*f 358
  //   43e c00 5*f 358 400 198 400 1d8 400 f f 358 466 1676 16b7 4*f 72*0 358 400 198 400 4*f 358 400 198
  //   400 1d8 5a8 f f 358 400 198 400 1d8 626 f f 358 400 398 63b 1000 f f f 358 43e c00 5*f 358 400 198
  //   400 1d8 400 f f 358 276 2b7 5*f 72*0 358 400 398 5c1 4*f 358 1e8 400 5*f 358 627 6*f 358 637 1000
  //   5*f 358 43f c00 5*f 358 400 198 400 1d8 400 f f 358 467 1676 16b7 4*f 72*0 358 400 1d8 400 4*f 358
  //   400 198 400 1d8 5e8 f f 358 400 198 400 1d8 627 f f 358 400 398 63b 1000 f f f 358 43f c00 5*f 358
  //   400 198 400 1d8 400 f f 358 276 2b7 5*f 72*0 358 400 398 401 4*f 358 28 400 5*f 358 620 6*f 358 630
  //   1000 5*f 358 438 c00 5*f 358 400 198 400 1d8 400 f f 358 440 1676 16b7 4*f 72*0 358 400 18 400 4*f
  //   358 400 198 400 1d8 428 f f 358 400 198 400 1d8 620 f f 358 400 398 63b 1000 f f f 358 438 c00 5*f
  //   358 400 198 400 1d8 400 f f 358 276 2b7 5*f 72*0 358 400 398 442 4*f 358 68 400 5*f 358 621 6*f 358
  //   631 1000 5*f 358 439 c00 5*f 358 400 198 400 1d8 400 f f 358 400 1676 16b7 4*f 72*0 358 400 58 400
  //   4*f 358 400 198 400 1d8 468 f f 358 400 198 400 1d8 621 f f 358 400 398 63b 1000 f f f 358 439 c00
  //   5*f 358 400 198 400 1d8 400 f f 358 276 2b7 5*f 72*0 358 400 398 482 4*f 358 a8 400 5*f 358 622 6*f
  //   358 632 1000 5*f 358 43a c00 5*f 358 400 198 400 1d8 400 f f 358 442 1676 16b7 4*f 72*0 358 400 98
  //   400 4*f 358 400 198 400 1d8 4a8 f f 358 400 198 400 1d8 622 f f 358 400 398 63b 1000 f f f 358 43a
  //   c00 5*f 358 400 198 400 1d8 400 f f 358 276 2b7 5*f 72*0 358 400 398 4c2 4*f 358 e8 400 5*f 358 623
  //   6*f 358 633 1000 5*f 358 43b c00 5*f 358 400 198 400 1d8 400 f f 358 443 1676 16b7 4*f 72*0 358 400
  //   d8 400 4*f 358 400 198 400 1d8 4e8 f f 358 400 198 400 1d8 623 f f 358 400 398 63b 1000 f f f 358
  //   43b c00 5*f 358 400 198 400 1d8 400 f f 358 276 2b7 5*f 72*0 358 400 398 502 4*f 358 128 400 5*f 358
  //   624 6*f 358 634 1000 5*f 358 43c c00 5*f 358 400 198 400 1d8 400 f f 358 444 1676 16b7 4*f 72*0 358
  //   400 118 400 4*f 358 400 198 400 1d8 528 f f 358 400 198 400 1d8 624 f f 358 400 398 63b 1000 f f f
  //   358 43c c00 5*f 358 400 198 400 1d8 400 f f 358 276 2b7 5*f 72*0 358 400 398 542 4*f 358 168 400 5*f
  //   358 625 6*f 358 635 1000 5*f 358 43d c00 5*f 358 400 198 400 1d8 400 f f 358 445 1676 16b7 4*f 72*0
  //   358 400 158 400 4*f 358 400 198 400 1d8 568 f f 358 400 198 400 1d8 625 f f 358 400 398 63b 1000 f f
  //   f 358 43d c00 5*f 358 400 198 400 1d8 400 f f 358 276 2b7 5*f 72*0 358 400 398 582 4*f 358 1a8 400
  //   5*f 358 626 6*f 358 636 1000 5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
  //   might remove
endmodule

module ram_assembly (
  input  CLOCK,
  input  [7:0] BIN,
  input  [15:0] AIN,
  input  MEM_READ,
  input  MEM_WRITE,
  input  nPC_AOUT,
  input  PC_CNT,
  input  nPC_LOAD_LOW,
  input  nPC_LOAD_HIGH,
  input  nMAR_AOUT,
  input  MAR_CNT,
  input  nMAR_LOAD_LOW,
  input  nMAR_LOAD_HIGH,
  input  nSP_AOUT,
  input  nSP_CNTUP,
  input  nSP_CNTDOWN,
  input  nSP_LOAD_LOW,
  input  nSP_LOAD_HIGH,
  input  nLOW_ATOB_EN,
  input  nHIGH_ATOB_EN,
  input  nRESET,
  output [7:0] BOUT,
  output [15:0] AOUT
);

  wire and_1_out, and_2_out, MEMORY_INTERACT, not_1_out, not_2_out, not_3_out, not_4_out, not_5_out,
       not_6_out, not_7_out, not_8_out, not_9_out;
  wire [7:0] ram_1_data, ram_2_data;

  not not_1 (not_1_out, AIN[15]);
  or or_1 (MEMORY_INTERACT, MEM_READ, MEM_WRITE);
  and and_1 (and_1_out, MEMORY_INTERACT, not_1_out);
  and and_2 (and_2_out, MEMORY_INTERACT, AIN[15]);
  not not_2 (not_2_out, and_1_out);
  not not_3 (not_3_out, and_2_out);
  not not_4 (not_4_out, MEM_WRITE);
  RAM #(.addrWidth(15), .asyncread("true"), .databus("bidir")) ram_1 (
    .addr(AIN[14:0]), .we(not_5_out), .oe(not_6_out), .clk(CLOCK), .data(ram_1_data));
  not not_5 (not_5_out, not_4_out);
  not not_6 (not_6_out, MEM_WRITE);
  not not_7 (not_7_out, MEM_WRITE);
  addr_counter PC (
    .CLOCK(CLOCK), .AIN({BIN, BIN}), .nBOUT_EN(nPC_AOUT), .nCLEAR(nRESET), .CNT_EN(PC_CNT),
    .nLOAD_EN_LOW(nPC_LOAD_LOW), .nLOAD_EN_HIGH(nPC_LOAD_HIGH), .AOUT(AOUT));  // open: Q
  addr_counter MAR (
    .CLOCK(CLOCK), .AIN({BIN, BIN}), .nBOUT_EN(nMAR_AOUT), .nCLEAR(nRESET), .CNT_EN(MAR_CNT),
    .nLOAD_EN_LOW(nMAR_LOAD_LOW), .nLOAD_EN_HIGH(nMAR_LOAD_HIGH), .AOUT(AOUT));  // open: Q
  addr_counter SP (
    .CLOCK(CLOCK), .AIN({BIN, BIN}), .nBOUT_EN(nSP_AOUT), .nCLEAR(nRESET), .CNT_EN(nSP_CNTUP),
    .nLOAD_EN_LOW(nSP_LOAD_LOW), .nLOAD_EN_HIGH(nSP_LOAD_HIGH), .AOUT(AOUT));  // open: Q
  RAM #(.addrWidth(15), .databus("bidir")) ram_2 (
    .addr(AIN[14:0]), .we(not_8_out), .oe(not_9_out), .clk(CLOCK), .data(ram_2_data));
  not not_8 (not_8_out, not_7_out);
  not not_9 (not_9_out, MEM_WRITE);
  // Probe on ram_1_data
  double_buffer double_buffer_1 (
    .N_ENABLE(not_2_out), .A_TO_B(not_4_out), .A_IN(ram_1_data), .B_IN(BIN), .B_OUT(BOUT), .A_OUT(ram_1_data));
  double_buffer double_buffer_2 (
    .N_ENABLE(not_3_out), .A_TO_B(not_7_out), .A_IN(ram_2_data), .B_IN(BIN), .B_OUT(BOUT), .A_OUT(ram_2_data));
  ttl_buffer ttl_buffer_1 (.N_ENABLE(nLOW_ATOB_EN), .inn(AIN[7:0]), .outt(BOUT));
  ttl_buffer ttl_buffer_2 (.N_ENABLE(nHIGH_ATOB_EN), .inn(AIN[15:8]), .outt(BOUT));

  // Other names for the same wires on the sheet: MEMORY_READ = MEM_READ; MEMORY_WRITE = MEM_WRITE

  // Notes on the sheet:
  //   nSP_LOAD_LOW: initial=0x1
  //   nSP_LOAD_HIGH: initial=0x1
  //   nPC_AOUT: initial=0x1
  //   nPC_LOAD_LOW: initial=0x1
  //   nPC_LOAD_HIGH: initial=0x1
  //   nMAR_AOUT: initial=0x1
  //   nMAR_LOAD_LOW: initial=0x1
  //   nMAR_LOAD_HIGH: initial=0x1
  //   nSP_AOUT: initial=0x1
  //   nLOW_ATOB_EN: initial=0x1
  //   nHIGH_ATOB_EN: initial=0x1
  //   nRESET: initial=0x1
  //   if either reading or writing
  //   need to implement
  //   if either reading or writing
  //   implictly defined by write/interact?
  //   first 32k bytes
  //   second 32k bytes
  //   program counter
  //   memory address register
  //   the actual chip has 3 state inputs with nCS (Chip select), so no buffers needed
  //   the actual chip has 3 state inputs with nCS (Chip select), so no buffers needed
  //   equivalent to CS in chip
  //   equivalent to CS in chip
  //   buffers from address to data bus
endmodule

module gp_counter (
  input  CLOCK,
  input  [7:0] BIN,
  input  nBIN_EN,
  input  nBOUT_EN,
  input  nCLEAR,
  input  CNT_EN,
  input  nLOAD_EN,
  output [7:0] BOUT,
  output [7:0] Q
);

  wire n74161_1_pin10, n74161_1_pin15, n74161_2_pin15;

  ttl_buffer ttl_buffer_1 (.N_ENABLE(nBIN_EN), .inn(BIN), .outt(BIN));
  ttl_buffer ttl_buffer_2 (.N_ENABLE(nBOUT_EN), .inn(Q), .outt(BOUT));
  _74161 #(.ShowInternalStructure("true")) u_74161_1 (
    .pin1(nCLEAR), .pin2(CLOCK), .pin3(BIN[0]), .pin4(BIN[1]), .pin5(BIN[2]), .pin6(BIN[3]), .pin7(CNT_EN),
    .pin15(n74161_1_pin15), .pin14(Q[0]), .pin13(Q[1]), .pin12(Q[2]), .pin11(Q[3]), .pin10(n74161_1_pin10),
    .pin9(nLOAD_EN));
  _74161 #(.ShowInternalStructure("true")) u_74161_2 (
    .pin1(nCLEAR), .pin2(CLOCK), .pin3(BIN[4]), .pin4(BIN[5]), .pin5(BIN[6]), .pin6(BIN[7]), .pin7(CNT_EN),
    .pin15(n74161_2_pin15), .pin14(Q[4]), .pin13(Q[5]), .pin12(Q[6]), .pin11(Q[7]), .pin10(n74161_1_pin15),
    .pin9(nLOAD_EN));
  // NoConnect on n74161_2_pin15
  // also tied to VCC on the sheet: n74161_1_pin10

  // Other names for the same wires on the sheet: D[7:0] = BIN; D0[3:0] = BIN[3:0]; D1[3:0] = BIN[7:4];
  //   Q0[3:0] = Q[3:0]; Q1[3:0] = Q[7:4]
endmodule

module addr_counter (
  input  CLOCK,
  input  [15:0] AIN,
  input  nBOUT_EN,
  input  nCLEAR,
  input  CNT_EN,
  input  nLOAD_EN_LOW,
  input  nLOAD_EN_HIGH,
  output [15:0] AOUT,
  output [15:0] Q
);

  wire n74161_1_pin10, n74161_1_pin15, n74161_2_pin15, n74161_3_pin15, n74161_4_pin15;

  _74161 #(.ShowInternalStructure("true")) u_74161_1 (
    .pin1(nCLEAR), .pin2(CLOCK), .pin3(AIN[0]), .pin4(AIN[1]), .pin5(AIN[2]), .pin6(AIN[3]), .pin7(CNT_EN),
    .pin15(n74161_1_pin15), .pin14(Q[0]), .pin13(Q[1]), .pin12(Q[2]), .pin11(Q[3]), .pin10(n74161_1_pin10),
    .pin9(nLOAD_EN_LOW));
  buffer_16 buffer_16_1 (.N_ENABLE(nBOUT_EN), .inn(Q), .outt(AOUT));
  _74161 #(.ShowInternalStructure("true")) u_74161_2 (
    .pin1(nCLEAR), .pin2(CLOCK), .pin3(AIN[4]), .pin4(AIN[5]), .pin5(AIN[6]), .pin6(AIN[7]), .pin7(CNT_EN),
    .pin15(n74161_2_pin15), .pin14(Q[4]), .pin13(Q[5]), .pin12(Q[6]), .pin11(Q[7]), .pin10(n74161_1_pin15),
    .pin9(nLOAD_EN_LOW));
  _74161 #(.ShowInternalStructure("true")) u_74161_3 (
    .pin1(nCLEAR), .pin2(CLOCK), .pin3(AIN[8]), .pin4(AIN[9]), .pin5(AIN[10]), .pin6(AIN[11]), .pin7(CNT_EN),
    .pin15(n74161_3_pin15), .pin14(Q[8]), .pin13(Q[9]), .pin12(Q[10]), .pin11(Q[11]), .pin10(n74161_2_pin15),
    .pin9(nLOAD_EN_HIGH));
  _74161 #(.ShowInternalStructure("true")) u_74161_4 (
    .pin1(nCLEAR), .pin2(CLOCK), .pin3(AIN[12]), .pin4(AIN[13]), .pin5(AIN[14]), .pin6(AIN[15]),
    .pin7(CNT_EN), .pin15(n74161_4_pin15), .pin14(Q[12]), .pin13(Q[13]), .pin12(Q[14]), .pin11(Q[15]),
    .pin10(n74161_3_pin15), .pin9(nLOAD_EN_HIGH));
  // NoConnect on n74161_4_pin15
  // also tied to VCC on the sheet: n74161_1_pin10

  // Other names for the same wires on the sheet: D[15:0] = AIN; D0[3:0] = AIN[3:0]; D1[3:0] = AIN[7:4];
  //   D2[3:0] = AIN[11:8]; D3[3:0] = AIN[15:12]; Q0[3:0] = Q[3:0]; Q1[3:0] = Q[7:4]; Q2[3:0] = Q[11:8];
  //   Q3[3:0] = Q[15:12]
endmodule

module buffer_16 (
  input  N_ENABLE,
  input  [15:0] inn,
  output [15:0] outt
);

  wire n74245_1_pin1, n74245_2_pin1;

  _74245 #(.ShowInternalStructure("true")) u_74245_1 (
    .pin1(n74245_1_pin1), .pin2(inn[0]), .pin3(inn[1]), .pin4(inn[2]), .pin5(inn[3]), .pin6(inn[4]),
    .pin7(inn[5]), .pin8(inn[6]), .pin9(inn[7]), .pin19(N_ENABLE), .pin18(outt[0]), .pin17(outt[1]),
    .pin16(outt[2]), .pin15(outt[3]), .pin14(outt[4]), .pin13(outt[5]), .pin12(outt[6]), .pin11(outt[7]));
  _74245 #(.ShowInternalStructure("true")) u_74245_2 (
    .pin1(n74245_2_pin1), .pin2(inn[8]), .pin3(inn[9]), .pin4(inn[10]), .pin5(inn[11]), .pin6(inn[12]),
    .pin7(inn[13]), .pin8(inn[14]), .pin9(inn[15]), .pin19(N_ENABLE), .pin18(outt[8]), .pin17(outt[9]),
    .pin16(outt[10]), .pin15(outt[11]), .pin14(outt[12]), .pin13(outt[13]), .pin12(outt[14]), .pin11(outt[15]));
  // also tied to VCC on the sheet: {n74245_1_pin1, n74245_2_pin1}

  // Notes on the sheet:
  //   N_ENABLE: initial=0x1
endmodule

module double_buffer (
  input  N_ENABLE,
  input  A_TO_B,
  input  [7:0] A_IN,
  input  [7:0] B_IN,
  output [7:0] B_OUT,
  output [7:0] A_OUT
);

  wire n74245_1_pin1, n74245_2_pin1, not_1_out, or_1_out, or_2_out;

  not not_1 (not_1_out, A_TO_B);
  or or_1 (or_1_out, N_ENABLE, not_1_out);
  or or_2 (or_2_out, N_ENABLE, A_TO_B);
  _74245 #(.ShowInternalStructure("true")) u_74245_1 (
    .pin1(n74245_1_pin1), .pin2(A_IN[0]), .pin3(A_IN[1]), .pin4(A_IN[2]), .pin5(A_IN[3]), .pin6(A_IN[4]),
    .pin7(A_IN[5]), .pin8(A_IN[6]), .pin9(A_IN[7]), .pin19(or_1_out), .pin18(B_OUT[0]), .pin17(B_OUT[1]),
    .pin16(B_OUT[2]), .pin15(B_OUT[3]), .pin14(B_OUT[4]), .pin13(B_OUT[5]), .pin12(B_OUT[6]), .pin11(B_OUT[7]));
  _74245 #(.ShowInternalStructure("true")) u_74245_2 (
    .pin1(n74245_2_pin1), .pin2(B_IN[0]), .pin3(B_IN[1]), .pin4(B_IN[2]), .pin5(B_IN[3]), .pin6(B_IN[4]),
    .pin7(B_IN[5]), .pin8(B_IN[6]), .pin9(B_IN[7]), .pin19(or_2_out), .pin18(A_OUT[0]), .pin17(A_OUT[1]),
    .pin16(A_OUT[2]), .pin15(A_OUT[3]), .pin14(A_OUT[4]), .pin13(A_OUT[5]), .pin12(A_OUT[6]), .pin11(A_OUT[7]));
  // also tied to VCC on the sheet: {n74245_2_pin1, n74245_1_pin1}

  // Notes on the sheet:
  //   N_ENABLE: initial=0x1
  //   A_TO_B: initial=0x1
endmodule

module counter8 (
  input  CLOCK,
  input  [7:0] D,
  input  nCLEAR,
  input  CNT_EN,
  input  nLOAD_EN,
  output [7:0] Q
);

  wire n74161_1_pin10, n74161_1_pin15, n74161_2_pin15;

  _74161 #(.ShowInternalStructure("true")) u_74161_1 (
    .pin1(nCLEAR), .pin2(CLOCK), .pin3(D[0]), .pin4(D[1]), .pin5(D[2]), .pin6(D[3]), .pin7(CNT_EN),
    .pin15(n74161_1_pin15), .pin14(Q[0]), .pin13(Q[1]), .pin12(Q[2]), .pin11(Q[3]), .pin10(n74161_1_pin10),
    .pin9(nLOAD_EN));
  Hex_Digit_Display L1 (.value(Q[7:4]));  // open: dp
  Hex_Digit_Display L0 (.value(Q[3:0]));  // open: dp
  _74161 #(.ShowInternalStructure("true")) u_74161_2 (
    .pin1(nCLEAR), .pin2(CLOCK), .pin3(D[4]), .pin4(D[5]), .pin5(D[6]), .pin6(D[7]), .pin7(CNT_EN),
    .pin15(n74161_2_pin15), .pin14(Q[4]), .pin13(Q[5]), .pin12(Q[6]), .pin11(Q[7]), .pin10(n74161_1_pin15),
    .pin9(nLOAD_EN));
  // NoConnect on n74161_2_pin15
  // also tied to VCC on the sheet: n74161_1_pin10

  // Other names for the same wires on the sheet: D0[3:0] = D[3:0]; D1[3:0] = D[7:4]; Q0[3:0] = Q[3:0];
  //   Q1[3:0] = Q[7:4]
endmodule

module counter4 (
  input  CLOCK,
  input  [3:0] D,
  input  nCLEAR,
  input  CNT_EN,
  input  nLOAD_EN,
  output [3:0] Q
);

  wire n74161_1_pin10, n74161_1_pin15;

  _74161 #(.ShowInternalStructure("true")) u_74161_1 (
    .pin1(nCLEAR), .pin2(CLOCK), .pin3(D[0]), .pin4(D[1]), .pin5(D[2]), .pin6(D[3]), .pin7(CNT_EN),
    .pin15(n74161_1_pin15), .pin14(Q[0]), .pin13(Q[1]), .pin12(Q[2]), .pin11(Q[3]), .pin10(n74161_1_pin10),
    .pin9(nLOAD_EN));
  // NoConnect on n74161_1_pin15
  Hex_Digit_Display #(.decimalPoint("false")) L_A1 (.value(Q));
  // also tied to VCC on the sheet: n74161_1_pin10
endmodule
